// Logisim project CPU_v24_bits_temp.circ as structural Verilog: 1 circuit, main circuit milo_optimized
module milo_optimized (
);

  wire adder_1_cout, and_1_out, and_2_out, and_3_out, and_5_out, clock_1_out, demultiplexer_1_out0,
       demultiplexer_1_out1, demultiplexer_1_out2, demultiplexer_1_out3, demultiplexer_1_out4,
       demultiplexer_1_out5, demultiplexer_1_out6, demultiplexer_1_out7, demultiplexer_1_out8,
       demultiplexer_1_out9, demultiplexer_1_out10, demultiplexer_1_out11, demultiplexer_1_out12,
       demultiplexer_1_out13, demultiplexer_1_out14, demultiplexer_1_out15, GLOBAL_RESET_out,
       multiplexer_4_out, multiplexer_5_out, multiplexer_6_out, multiplexer_11_out, not_2_out, or_1_out,
       or_5_out, or_6_out, subtractor_1_bout, xnor_1_out, xor_1_out, xor_2_out, xor_3_out;
  wire [1:0] demultiplexer_4_out3_2;
  wire [2:0] ROM_1_data_9;
  wire [3:0] FLAGS_q, ROM_1_data_3, ROM_1_data_4, ROM_1_data_5, ROM_1_data_6, ROM_1_data_7, ROM_1_data_8;
  wire [3:1] comparator_1_eq;
  wire [3:3] ROM_1_data_10;
  wire [4:0] demultiplexer_3_out6, demultiplexer_3_out7;
  wire [11:0] demultiplexer_4_out1, demultiplexer_4_out2, demultiplexer_4_out3, ROM_1_data_2;
  wire [15:0] STACK_POINTER_q;
  wire [22:0] multiplexer_1_out;
  wire [23:0] adder_1_out, adder_2_out, and_4_out, controlled_buffer_1_out, controlled_buffer_2_out,
       demultiplexer_2_out0, demultiplexer_2_out1, demultiplexer_2_out2, demultiplexer_2_out3,
       demultiplexer_2_out4, demultiplexer_2_out5, demultiplexer_2_out6, demultiplexer_2_out7,
       demultiplexer_3_out0, demultiplexer_3_out1, demultiplexer_3_out2, demultiplexer_3_out3,
       demultiplexer_3_out4, multiplexer_2_out, multiplexer_3_out, multiplexer_7_out, multiplexer_8_out,
       multiplexer_9_out, multiplexer_10_out, multiplexer_12_out, multiplexer_13_out, not_1_out, or_4_out,
       PROGRAM_COUNTER_q, R0_q, R1_q, R2_q, R3_q, R4_q, R5_q, R6_q, R7_q, R8_q, R9_q, R10_q, R11_q, R12_q,
       R13_q, R14_q, R15_q, RAM_1_dout, RAM_2_dout, ROM_1_data, shifter_1_out, shifter_2_out,
       subtractor_1_out, xor_4_out;
  wire [23:5] demultiplexer_3_out6_2, demultiplexer_3_out7_2;

  assign controlled_buffer_1_out = demultiplexer_4_out1[1] ? multiplexer_2_out : 24'bz;  // Controlled_Buffer controlled_buffer_1
  or or_1 (or_1_out, demultiplexer_4_out2[1], demultiplexer_4_out1[0]);
  Demultiplexer #(.select(4)) demultiplexer_1 (
    .out0(demultiplexer_1_out0), .out1(demultiplexer_1_out1), .out2(demultiplexer_1_out2),
    .out3(demultiplexer_1_out3), .out4(demultiplexer_1_out4), .out5(demultiplexer_1_out5),
    .out6(demultiplexer_1_out6), .out7(demultiplexer_1_out7), .out8(demultiplexer_1_out8),
    .out9(demultiplexer_1_out9), .out10(demultiplexer_1_out10), .out11(demultiplexer_1_out11),
    .out12(demultiplexer_1_out12), .out13(demultiplexer_1_out13), .out14(demultiplexer_1_out14),
    .out15(demultiplexer_1_out15), .in(or_1_out), .sel(ROM_1_data_5));
  and and_1 (and_1_out, xor_1_out, xnor_1_out);
  assign controlled_buffer_2_out = demultiplexer_4_out1[1] ? multiplexer_3_out : 24'bz;  // Controlled_Buffer controlled_buffer_2
  Demultiplexer #(.select(3), .width(24)) demultiplexer_2 (
    .out0(demultiplexer_2_out0), .out1(demultiplexer_2_out1), .out2(demultiplexer_2_out2),
    .out3(demultiplexer_2_out3), .out4(demultiplexer_2_out4), .out5(demultiplexer_2_out5),
    .out6(demultiplexer_2_out6), .out7(demultiplexer_2_out7), .in(controlled_buffer_2_out),
    .sel(demultiplexer_4_out1[6:4]));
  Demultiplexer #(.select(3), .width(24)) demultiplexer_3 (
    .out0(demultiplexer_3_out0), .out1(demultiplexer_3_out1), .out2(demultiplexer_3_out2),
    .out3(demultiplexer_3_out3), .out4(demultiplexer_3_out4),
    .out6({demultiplexer_3_out6_2, demultiplexer_3_out6}),
    .out7({demultiplexer_3_out7_2, demultiplexer_3_out7}), .in(controlled_buffer_1_out),
    .sel(demultiplexer_4_out1[6:4]));  // open: out5
  Button GLOBAL_RESET (.out(GLOBAL_RESET_out));
  Clock clock_1 (.out(clock_1_out));
  xor xor_1 (xor_1_out, demultiplexer_2_out0[23], demultiplexer_2_out0[23]);
  xnor xnor_1 (xnor_1_out, demultiplexer_3_out0[23], demultiplexer_2_out0[23]);
  and and_2 (and_2_out, FLAGS_q[2], demultiplexer_4_out1[3]);
  Register #(.width(24)) R0 (
    .D(multiplexer_13_out), .en(demultiplexer_1_out0), .Q(R0_q), .clk(clock_1_out), .clr(GLOBAL_RESET_out));
  Register #(.width(24)) R8 (
    .D(multiplexer_13_out), .en(demultiplexer_1_out8), .Q(R8_q), .clk(clock_1_out), .clr(GLOBAL_RESET_out));
  or or_2 (comparator_1_eq[3], and_1_out, and_3_out);
  xor xor_2 (xor_2_out, demultiplexer_2_out0[23], demultiplexer_2_out1[23]);
  xor xor_3 (xor_3_out, demultiplexer_2_out1[23], demultiplexer_3_out1[23]);
  Register #(.width(24)) R1 (
    .D(multiplexer_13_out), .en(demultiplexer_1_out1), .Q(R1_q), .clk(clock_1_out), .clr(GLOBAL_RESET_out));
  Register #(.width(24)) R9 (
    .D(multiplexer_13_out), .en(demultiplexer_1_out9), .Q(R9_q), .clk(clock_1_out), .clr(GLOBAL_RESET_out));
  and and_3 (and_3_out, xor_2_out, xor_3_out);
  or or_3 (comparator_1_eq[2], adder_1_cout, subtractor_1_bout);
  Adder #(.width(24)) adder_1 (
    .a(demultiplexer_2_out0), .b(demultiplexer_3_out0), .out(adder_1_out), .cin(and_2_out),
    .cout(adder_1_cout));
  Subtractor #(.width(24)) subtractor_1 (
    .a(demultiplexer_2_out1), .b(demultiplexer_3_out1), .out(subtractor_1_out), .bin(and_2_out),
    .bout(subtractor_1_bout));
  assign and_4_out = demultiplexer_2_out2 & demultiplexer_3_out2;  // AND_Gate and_4, 24 bits wide
  assign or_4_out = demultiplexer_2_out3 | demultiplexer_3_out3;  // OR_Gate or_4, 24 bits wide
  assign xor_4_out = demultiplexer_2_out4 ^ demultiplexer_3_out4;  // XOR_Gate xor_4, 24 bits wide
  assign not_1_out = ~demultiplexer_2_out5;  // NOT_Gate not_1, 24 bits wide
  Shifter #(.width(24)) shifter_1 (.in(demultiplexer_2_out6), .\dist (demultiplexer_3_out6), .out(shifter_1_out));
  Shifter #(.shift("lr"), .width(24)) shifter_2 (
    .in(demultiplexer_2_out7), .\dist (demultiplexer_3_out7), .out(shifter_2_out));
  Register #(.width(24)) R2 (
    .D(multiplexer_13_out), .en(demultiplexer_1_out2), .Q(R2_q), .clk(clock_1_out), .clr(GLOBAL_RESET_out));
  Register #(.width(24)) R10 (
    .D(multiplexer_13_out), .en(demultiplexer_1_out10), .Q(R10_q), .clk(clock_1_out), .clr(GLOBAL_RESET_out));
  Comparator #(.mode("unsigned"), .width(24)) comparator_1 (
    .a({demultiplexer_2_out0[23], multiplexer_1_out}), .b({24{1'b0}}), .eq(comparator_1_eq[1]));  // open: gt, lt
  Multiplexer #(.select(3), .width(24)) multiplexer_1 (
    .in0(adder_1_out), .in1(subtractor_1_out), .in2(and_4_out), .in3(or_4_out), .in4(xor_4_out),
    .in5(not_1_out), .in6(shifter_1_out), .in7(shifter_2_out),
    .out({demultiplexer_2_out0[23], multiplexer_1_out}), .sel(demultiplexer_4_out1[6:4]));
  Register #(.width(24)) R3 (
    .D(multiplexer_13_out), .en(demultiplexer_1_out3), .Q(R3_q), .clk(clock_1_out), .clr(GLOBAL_RESET_out));
  Register #(.width(24)) R11 (
    .D(multiplexer_13_out), .en(demultiplexer_1_out11), .Q(R11_q), .clk(clock_1_out), .clr(GLOBAL_RESET_out));
  Register #(.width(24)) R4 (
    .D(multiplexer_13_out), .en(demultiplexer_1_out4), .Q(R4_q), .clk(clock_1_out), .clr(GLOBAL_RESET_out));
  Register #(.width(24)) R12 (
    .D(multiplexer_13_out), .en(demultiplexer_1_out12), .Q(R12_q), .clk(clock_1_out), .clr(GLOBAL_RESET_out));
  Register #(.width(4)) FLAGS (
    .D({comparator_1_eq, demultiplexer_2_out0[23]}), .en(demultiplexer_4_out1[2]), .Q(FLAGS_q),
    .clk(clock_1_out), .clr(GLOBAL_RESET_out));
  Register #(.width(24)) R5 (
    .D(multiplexer_13_out), .en(demultiplexer_1_out5), .Q(R5_q), .clk(clock_1_out), .clr(GLOBAL_RESET_out));
  Register #(.width(24)) R6 (
    .D(multiplexer_13_out), .en(demultiplexer_1_out6), .Q(R6_q), .clk(clock_1_out), .clr(GLOBAL_RESET_out));
  Register #(.width(24)) R13 (
    .D(multiplexer_13_out), .en(demultiplexer_1_out13), .Q(R13_q), .clk(clock_1_out), .clr(GLOBAL_RESET_out));
  Register #(.width(24)) R14 (
    .D(multiplexer_13_out), .en(demultiplexer_1_out14), .Q(R14_q), .clk(clock_1_out), .clr(GLOBAL_RESET_out));
  Counter #(.max('hffff), .width(16)) STACK_POINTER (
    .count(demultiplexer_4_out3[4]), .Q(STACK_POINTER_q), .up(demultiplexer_4_out3[3]), .clk(clock_1_out),
    .clr(GLOBAL_RESET_out));  // open: load, D, carry
  Register #(.width(24)) R7 (
    .D(multiplexer_13_out), .en(demultiplexer_1_out7), .Q(R7_q), .clk(clock_1_out), .clr(GLOBAL_RESET_out));
  Register #(.width(24)) R15 (
    .D(multiplexer_13_out), .en(demultiplexer_1_out15), .Q(R15_q), .clk(clock_1_out), .clr(GLOBAL_RESET_out));
  Multiplexer #(.select(2), .width(24)) multiplexer_2 (
    .in0(multiplexer_9_out), .in1(RAM_1_dout), .in2(ROM_1_data), .out(multiplexer_2_out),
    .sel(ROM_1_data_3[3:2]));  // open: in3
  Multiplexer #(.select(2), .width(24)) multiplexer_3 (
    .in0(multiplexer_8_out), .in1(RAM_1_dout), .in2(ROM_1_data), .out(multiplexer_3_out),
    .sel(ROM_1_data_3[1:0]));  // open: in3
  Multiplexer #(.select(2)) multiplexer_4 (
    .in0(FLAGS_q[0]), .in1(FLAGS_q[1]), .in2(FLAGS_q[2]), .in3(FLAGS_q[3]), .out(multiplexer_4_out),
    .sel(demultiplexer_4_out3_2));
  Multiplexer multiplexer_5 (
    .in0(multiplexer_4_out), .in1(not_2_out), .out(multiplexer_5_out), .sel(demultiplexer_4_out3[6]));
  not not_2 (not_2_out, multiplexer_6_out);
  Multiplexer #(.select(2)) multiplexer_6 (
    .in0(FLAGS_q[0]), .in1(FLAGS_q[1]), .in2(FLAGS_q[2]), .in3(FLAGS_q[3]), .out(multiplexer_6_out),
    .sel(demultiplexer_4_out3_2));
  RAM #(.addrWidth(16), .dataWidth(24), .enables("line")) RAM_2 (
    .addr(STACK_POINTER_q), .we(demultiplexer_4_out3[2]), .clk(clock_1_out), .din(adder_2_out),
    .dout(RAM_2_dout));
  Adder #(.width(24)) adder_2 (.a(24'h1), .b(PROGRAM_COUNTER_q), .out(adder_2_out));  // open: cin, cout
  Multiplexer #(.select(3), .width(24)) multiplexer_7 (
    .in0(R0_q), .in1(R1_q), .in2(R2_q), .in3(R3_q), .in4(R4_q), .in5(R5_q), .in6(R6_q), .in7(R7_q),
    .out(multiplexer_7_out), .sel(ROM_1_data_8[2:0]));
  and and_5 (and_5_out, demultiplexer_4_out3[5], multiplexer_5_out);
  Multiplexer #(.select(4), .width(24)) multiplexer_8 (
    .in0(R0_q), .in1(R1_q), .in2(R2_q), .in3(R3_q), .in4(R4_q), .in5(R5_q), .in6(R6_q), .in7(R7_q),
    .in8(R8_q), .in9(R9_q), .in10(R10_q), .in11(R11_q), .in12(R12_q), .in13(R13_q), .in14(R14_q),
    .in15(R15_q), .out(multiplexer_8_out), .sel(ROM_1_data_7));
  Multiplexer #(.select(4), .width(24)) multiplexer_9 (
    .in0(R0_q), .in1(R1_q), .in2(R2_q), .in3(R3_q), .in4(R4_q), .in5(R5_q), .in6(R6_q), .in7(R7_q),
    .in8(R8_q), .in9(R9_q), .in10(R10_q), .in11(R11_q), .in12(R12_q), .in13(R13_q), .in14(R14_q),
    .in15(R15_q), .out(multiplexer_9_out), .sel(ROM_1_data_6));
  or or_5 (or_5_out, demultiplexer_4_out3[0], and_5_out);
  Multiplexer #(.width(24)) multiplexer_10 (
    .in0(ROM_1_data), .in1(RAM_2_dout), .out(multiplexer_10_out), .sel(demultiplexer_4_out3[1]));
  ROM #(.addrWidth(24), .dataWidth(64)) ROM_1 (
    .addr(PROGRAM_COUNTER_q),
    .data({ROM_1_data_10[3], ROM_1_data_9, ROM_1_data_8, ROM_1_data_7, ROM_1_data_6, ROM_1_data_5, ROM_1_data_4, ROM_1_data_3, ROM_1_data_2, ROM_1_data}));
  Counter #(.max('hffffff), .width(24)) PROGRAM_COUNTER (
    .load(or_5_out), .D(multiplexer_10_out), .count(multiplexer_11_out), .Q(PROGRAM_COUNTER_q), .up(1'b1),
    .clk(clock_1_out), .clr(GLOBAL_RESET_out));  // open: carry
  Multiplexer multiplexer_11 (.in0(1'b1), .out(multiplexer_11_out), .sel(demultiplexer_4_out3[9]));  // open: in1
  Multiplexer #(.width(24)) multiplexer_12 (
    .in0(multiplexer_7_out), .in1(ROM_1_data), .out(multiplexer_12_out), .sel(ROM_1_data_8[3]));
  or or_6 (or_6_out, demultiplexer_4_out2[0], demultiplexer_4_out1[7]);
  RAM #(.addrWidth(24), .dataWidth(24), .enables("line")) RAM_1 (
    .addr(multiplexer_12_out), .we(or_6_out), .clk(clock_1_out), .din(multiplexer_13_out), .dout(RAM_1_dout));
  Multiplexer #(.select(3), .width(24)) multiplexer_13 (
    .in0({demultiplexer_2_out0[23], multiplexer_1_out}), .in1(multiplexer_9_out), .in2(RAM_1_dout),
    .in3(ROM_1_data), .out(multiplexer_13_out), .sel(ROM_1_data_4[2:0]));  // open: in4, in5, in6, in7
  Demultiplexer #(.select(3), .width(12)) demultiplexer_4 (
    .out1(demultiplexer_4_out1), .out2(demultiplexer_4_out2),
    .out3({demultiplexer_4_out3[11:9], demultiplexer_4_out3_2, demultiplexer_4_out3[6:0]}),
    .in(ROM_1_data_2), .sel(ROM_1_data_9));  // open: out0, out4, out5, out6, out7

  // Notes on the sheet:
  //   BUS_B
  //   BUS_A
  //   BUS_C
  //   ALU_CONTROL
  //   PC_CONTROL
  //   contents of ROM_1 (hex, n*v repeats v):
  //   200003000200000a 2000130002000003 1001200003000000 2802010001000000 101030000b000000
  //   2803010001000001 1001400013000000 2804010001000002 101050001b000000 2805010001000003
  //   1010600023000000 2806010001000004 1001700033000000 2807010001000005 1010800043000000
  //   2808010001000006 1010900063000000 2809010001000007 1001a00073000000 280a010001000008
  //   1010b00053000000 280b010001000009 1001c0200300000a 280c01000100000a 1010d08003000003
  //   280d01000100000b 1000e0a003000005 280e01000100000c 1010f04003000000 280f01000100000d
  //   1001f01003000000 280f01000100000e 1000f05003000000 280f01000100000f 1000f06003000003
  //   280f010001000010 1000f09003000003 280f010001000011 1812000082000012 2000230002000013
  //   1201002082000003 2000230002000014 1210008082000003 180000a082000015 2000230002000016
  //   1201001082000000 2000230002000017 1210004082000000 1800006082000018 1800009082000019
  //   200023000200001a 1200005082000000 1000005016000000
  //   FINE_CTRL
  //   REGS_CTRL
  //   MAR_CTRL
  //   OPCODE
  //   IMMEDIATE
  //   BUS_CTRL
endmodule
